# Fritzing sketch Prototype (saved by Fritzing 0.9.9b)
circuit board: 9.98949cm x 3.36168cm
breadboards: 1

parts:
  R1-100K-Thermistor = Resistor [tolerance=±5% power=0.25 resistance=100k package=THT]
  HI-LINK = HLK-PM01
  J1-AC = Screw terminal - 2 pins [package=THT]
  J3-Thermistor = Screw terminal - 2 pins [package=THT]
  JP2 = Header 12 [package=1x12_machine-pin-header_lock.004]
  J5-D/T = screw terminal, 3 pins
  J4-GND = Screw terminal - 2 pins [package=THT]
  J2 = Screw terminal - 2 pins [package=THT]
  R2-220h-Btn-Touch = Resistor [tolerance=±5% power=0.25 resistance=220 package=THT]
  J1 = Screw terminal - 2 pins [package=THT]
  J6-LED = Screw terminal - 2 pins [package=THT]
  J7-Relay = Dagu DGServo 9g header connector (female) [package=THT]
  JP1 = Header 12 [package=1x12_machine-pin-header_lock.004]

nets:
  N1: R1-100K-Thermistor.Pin_0, HI-LINK.-Vo, JP2.4, J4-GND.pin2, J1.pin1, J7-Relay.pulse, JP1.2
  N2: R1-100K-Thermistor.Pin_1, J3-Thermistor.pin2, JP1.8
  N3: HI-LINK.AC#0, J1-AC.pin2
  N4: HI-LINK.AC#1, J1-AC.pin1
  N5: HI-LINK.+Vo, J1.pin2, J7-Relay.gnd, JP1.1
  N6: J3-Thermistor.pin1, J2.pin1, JP1.4
  N7: JP2.3, J4-GND.pin1, R2-220h-Btn-Touch.Pin_0
  N8: JP2.5, J5-D/T.pin1
  N9: JP2.6, J5-D/T.pin2
  N10: JP2.7, J5-D/T.pin3, R2-220h-Btn-Touch.Pin_1
  N11: JP2.9, J6-LED.pin1
  N12: JP2.10, J6-LED.pin2
  N13: JP2.11, J7-Relay.Vcc
  N14: J2.pin2, JP1.3

notes:
  GND
  2-GND
  SDA
  SCL
  TCH
  LED1
  LED2
  RAW
  VCC
  RST
  VCC-T
  A0-T
  INPUT ~100-240ac
  OUTPUT 5V DC
